// Logisim project CPU8_1411(Dumy).circ as structural Verilog
module _01_nand_gate (
  input  A,
  input  B,
  output Y_and,
  output Y_or,
  output Y_not,
  output Y_nand,
  output Y_nor,
  output Y_xor,
  output Y_xor_2,
  output Y_buffer
);

  wire nand_1_out, nand_2_out, nand_4_out, nand_5_out, nand_6_out, nand_7_out, nand_9_out, nand_10_out,
       nand_11_out, nand_12_out, nand_13_out, nand_14_out, nand_18_out, nand_21_out;

  nand nand_1 (nand_1_out, A, A);
  nand nand_2 (nand_2_out, B, B);
  nand nand_3 (Y_not, A, A);
  nand nand_4 (nand_4_out, A, A);
  nand nand_5 (nand_5_out, B, B);
  nand nand_6 (nand_6_out, A, A);
  nand nand_7 (nand_7_out, A, B);
  nand nand_8 (Y_nand, A, B);
  nand nand_9 (nand_9_out, A, nand_10_out);
  nand nand_10 (nand_10_out, A, B);
  nand nand_11 (nand_11_out, nand_10_out, B);
  nand nand_12 (nand_12_out, A, nand_13_out);
  nand nand_13 (nand_13_out, A, B);
  nand nand_14 (nand_14_out, nand_13_out, B);
  nand nand_15 (Y_buffer, nand_6_out, nand_6_out);
  nand nand_16 (Y_and, nand_7_out, nand_7_out);
  nand nand_17 (Y_or, nand_1_out, nand_2_out);
  nand nand_18 (nand_18_out, nand_4_out, nand_5_out);
  nand nand_19 (Y_nor, nand_18_out, nand_18_out);
  nand nand_20 (Y_xor, nand_9_out, nand_11_out);
  nand nand_21 (nand_21_out, nand_12_out, nand_14_out);
  nand nand_22 (Y_xor_2, nand_21_out, nand_21_out);
endmodule

module _02_1M (
  input  i,
  input  i_2,
  output o
);

  wire nand_1_out, nand_2_out, nand_4_out;

  nand nand_1 (nand_1_out, i, i_2);
  nand nand_2 (nand_2_out, nand_1_out, i_2);
  nand nand_3 (o, nand_1_out, nand_4_out);
  nand nand_4 (nand_4_out, o, nand_2_out);
endmodule

module _02_1test (
  input  S,
  input  i,
  input  I_2,
  input  s_2,
  output O,
  output o_2
);

  D_Flip_Flop #(.trigger("high")) d_ff_1 (.clk(S), .D(I_2), .Q(O));  // open: Qn, preset, reset
  Register #(.trigger("high"), .width(1)) register_1 (.D(i), .en(s_2), .Q(o_2), .clk(1'b1));  // open: clr
endmodule

module _03_8register (
  input  [7:0] i,
  input  set,
  output [7:0] o
);

  Register #(.trigger("high")) register_1 (.D(i), .en(set), .Q(o), .clk(1'b1));  // open: clr
endmodule

module _04_1_Enabler (
  input  [7:0] i,
  input  e,
  output [7:0] o
);

  assign o = e ? i : 8'bz;  // Controlled_Buffer controlled_buffer_1
endmodule

module _3_2_BReg (
  input  [7:0] i,
  input  s,
  input  e,
  output [7:0] o
);

  wire [7:0] n03_8register_1_o;

  _03_8register u_03_8register_1 (.i(i), .set(s), .o(n03_8register_1_o));
  _04_1_Enabler u_04_1_enabler_1 (.i(n03_8register_1_o), .e(e), .o(o));
endmodule
