// Logisim project CPU8_1411.circ as structural Verilog
module _01_nand_gate (
  input  A,
  input  B,
  output Y_and,
  output Y_or,
  output Y_not,
  output Y_nand,
  output Y_nor,
  output Y_xor,
  output Y_xor_2,
  output Y_buffer
);

  wire nand_1_out, nand_2_out, nand_4_out, nand_5_out, nand_6_out, nand_7_out, nand_9_out, nand_10_out,
       nand_11_out, nand_12_out, nand_13_out, nand_14_out, nand_18_out, nand_21_out;

  nand nand_1 (nand_1_out, A, A);
  nand nand_2 (nand_2_out, B, B);
  nand nand_3 (Y_not, A, A);
  nand nand_4 (nand_4_out, A, A);
  nand nand_5 (nand_5_out, B, B);
  nand nand_6 (nand_6_out, A, A);
  nand nand_7 (nand_7_out, A, B);
  nand nand_8 (Y_nand, A, B);
  nand nand_9 (nand_9_out, A, nand_10_out);
  nand nand_10 (nand_10_out, A, B);
  nand nand_11 (nand_11_out, nand_10_out, B);
  nand nand_12 (nand_12_out, A, nand_13_out);
  nand nand_13 (nand_13_out, A, B);
  nand nand_14 (nand_14_out, nand_13_out, B);
  nand nand_15 (Y_buffer, nand_6_out, nand_6_out);
  nand nand_16 (Y_and, nand_7_out, nand_7_out);
  nand nand_17 (Y_or, nand_1_out, nand_2_out);
  nand nand_18 (nand_18_out, nand_4_out, nand_5_out);
  nand nand_19 (Y_nor, nand_18_out, nand_18_out);
  nand nand_20 (Y_xor, nand_9_out, nand_11_out);
  nand nand_21 (nand_21_out, nand_12_out, nand_14_out);
  nand nand_22 (Y_xor_2, nand_21_out, nand_21_out);
endmodule

module _02_1M (
  input  i,
  input  i_2,
  output o
);

  wire nand_1_out, nand_2_out, nand_4_out;

  nand nand_1 (nand_1_out, i, i_2);
  nand nand_2 (nand_2_out, nand_1_out, i_2);
  nand nand_3 (o, nand_1_out, nand_4_out);
  nand nand_4 (nand_4_out, o, nand_2_out);
endmodule

module _02_1test (
  input  S,
  input  i,
  input  I_2,
  input  s_2,
  output O,
  output o_2
);

  D_Flip_Flop #(.trigger("high")) d_ff_1 (.clk(S), .D(I_2), .Q(O));  // open: Qn, preset, reset
  Register #(.trigger("high"), .width(1)) register_1 (.D(i), .en(s_2), .Q(o_2), .clk(1'b1));  // open: clr
endmodule

module _03_8register (
  input  [7:0] i,
  input  set,
  output [7:0] o
);

  Register #(.trigger("high")) register_1 (.D(i), .en(set), .Q(o), .clk(1'b1));  // open: clr
endmodule

module _03_1_Enabler (
  input  [7:0] i,
  input  e,
  output [7:0] o
);

  assign o = e ? i : 8'bz;  // Controlled_Buffer controlled_buffer_1
endmodule

module _3_2_8Reg (
  input  [7:0] i,
  input  s,
  input  e,
  output [7:0] o
);

  wire [7:0] n03_8register_1_o;

  _03_8register u_03_8register_1 (.i(i), .set(s), .o(n03_8register_1_o));
  _03_1_Enabler u_03_1_enabler_1 (.i(n03_8register_1_o), .e(e), .o(o));
endmodule

module _03_3_BusTest (
  input  in_1,
  input  in_2,
  input  in_3,
  input  in_4,
  input  [7:0] in_5,
  output [7:0] out_6,
  output [7:0] out_7,
  output [7:0] out_8
);

  wire nor_1_out;

  nor nor_1 (nor_1_out, in_2, in_1);
  assign out_8 = nor_1_out ? in_5 : 8'bz;  // Controlled_Buffer controlled_buffer_1
  _3_2_8Reg RA (.i(out_8), .s(in_3), .e(in_1), .o(out_6));
  assign out_8 = in_1 ? out_6 : 8'bz;  // Controlled_Buffer controlled_buffer_2
  _3_2_8Reg u_3_2_8reg_1 (.i(out_8), .s(in_4), .e(in_2), .o(out_7));
  assign out_8 = in_2 ? out_7 : 8'bz;  // Controlled_Buffer controlled_buffer_3
endmodule

module Enabler (
  input  [7:0] i,
  input  e,
  output [7:0] o
);

  assign o = e ? i : 8'bz;  // Controlled_Buffer controlled_buffer_1
endmodule

module Adder (
  input  Ci,
  input  [7:0] A,
  input  [7:0] B,
  output [7:0] S,
  output Co
);

  Adder_part adder_1 (.a(A), .b(B), .out(S), .cin(Ci), .cout(Co));
endmodule

module SHR (
  input  [7:0] i,
  input  si,
  output so,
  output [7:0] o
);

  wire [7:1] register_1_q;

  Register #(.trigger("high")) register_1 (.D(i), .en(1'b1), .Q({register_1_q, so}), .clk(1'b1));  // open: clr
  Register #(.trigger("high")) register_2 (.D({si, register_1_q}), .en(1'b1), .Q(o), .clk(1'b1));  // open: clr
endmodule

module SHL (
  input  si,
  input  [7:0] i,
  output [7:0] o,
  output so
);

  wire [6:0] register_1_q;

  Register #(.trigger("high")) register_1 (.D(i), .en(1'b1), .Q({so, register_1_q}), .clk(1'b1));  // open: clr
  Register #(.trigger("high")) register_2 (.D({register_1_q, si}), .en(1'b1), .Q(o), .clk(1'b1));  // open: clr
endmodule

module invuter (
  input  [7:0] i,
  output [7:0] o
);

  assign o = ~i;  // NOT_Gate not_1, 8 bits wide
endmodule

module Ander (
  input  [7:0] A,
  input  [7:0] B,
  output [7:0] O
);

  assign O = A & B;  // AND_Gate and_1, 8 bits wide
endmodule

module Orer (
  input  [7:0] A,
  input  [7:0] B,
  output [7:0] O
);

  assign O = A | B;  // OR_Gate or_1, 8 bits wide
endmodule

module Xorer1 (
  input  S_i,
  input  L_i,
  input  A,
  input  B,
  output O,
  output S_o,
  output L_o
);

  wire and_2_out, not_1_out;

  xor xor_1 (O, A, B);
  not not_1 (not_1_out, O);
  and and_1 (S_o, not_1_out, S_i);
  and and_2 (and_2_out, S_i, A, O);
  or or_1 (L_o, and_2_out, L_i);
endmodule

module Xorer8 (
  input  [7:0] A,
  input  [7:0] B,
  output [7:0] O,
  output S_O,
  output L_O
);

  wire xorer1_1_l_o, xorer1_1_s_o, xorer1_2_l_o, xorer1_2_s_o, xorer1_3_l_o, xorer1_3_s_o, xorer1_4_l_o,
       xorer1_4_s_o, xorer1_5_l_o, xorer1_5_s_o, xorer1_6_l_o, xorer1_6_s_o, xorer1_7_l_o, xorer1_7_s_o;

  Xorer1 xorer1_1 (.S_i(1'b1), .L_i(1'b0), .A(A[7]), .B(B[7]), .O(O[7]), .S_o(xorer1_1_s_o), .L_o(xorer1_1_l_o));
  Xorer1 xorer1_2 (
    .S_i(xorer1_1_s_o), .L_i(xorer1_1_l_o), .A(A[6]), .B(B[6]), .O(O[6]), .S_o(xorer1_2_s_o),
    .L_o(xorer1_2_l_o));
  Xorer1 xorer1_3 (
    .S_i(xorer1_2_s_o), .L_i(xorer1_2_l_o), .A(A[5]), .B(B[5]), .O(O[5]), .S_o(xorer1_3_s_o),
    .L_o(xorer1_3_l_o));
  Xorer1 xorer1_4 (
    .S_i(xorer1_3_s_o), .L_i(xorer1_3_l_o), .A(A[4]), .B(B[4]), .O(O[4]), .S_o(xorer1_4_s_o),
    .L_o(xorer1_4_l_o));
  Xorer1 xorer1_5 (
    .S_i(xorer1_4_s_o), .L_i(xorer1_4_l_o), .A(A[3]), .B(B[3]), .O(O[3]), .S_o(xorer1_5_s_o),
    .L_o(xorer1_5_l_o));
  Xorer1 xorer1_6 (
    .S_i(xorer1_5_s_o), .L_i(xorer1_5_l_o), .A(A[2]), .B(B[2]), .O(O[2]), .S_o(xorer1_6_s_o),
    .L_o(xorer1_6_l_o));
  Xorer1 xorer1_7 (
    .S_i(xorer1_6_s_o), .L_i(xorer1_6_l_o), .A(A[1]), .B(B[1]), .O(O[1]), .S_o(xorer1_7_s_o),
    .L_o(xorer1_7_l_o));
  Xorer1 xorer1_8 (.S_i(xorer1_7_s_o), .L_i(xorer1_7_l_o), .A(A[0]), .B(B[0]), .O(O[0]), .S_o(S_O), .L_o(L_O));
endmodule

module Zeroer (
  input  [7:0] in,
  output out
);

  nor nor_1 (out, in[0], in[1], in[2], in[3], in[4], in[5], in[6], in[7]);
endmodule

module ALU (
  input  [7:0] a,
  input  [7:0] b,
  input  ci,
  input  [2:0] op,
  output a_b,
  output a_b_2,
  output zero,
  output [7:0] out,
  output co
);

  wire adder_1_co, c_ad, c_sl, c_sr, decoder_1_out0, decoder_1_out1, decoder_1_out2, decoder_1_out3,
       decoder_1_out4, decoder_1_out5, decoder_1_out6, decoder_1_out7, shl_1_so, shr_1_so;
  wire [7:0] adder_1_s, ander_1_o, enabler_4_o, invuter_1_o, orer_1_o, shl_1_o, shr_1_o, xorer8_1_o;

  Xorer8 xorer8_1 (.A(a), .B(b), .O(xorer8_1_o), .S_O(a_b), .L_O(a_b_2));
  Orer orer_1 (.A(a), .B(b), .O(orer_1_o));
  Ander ander_1 (.A(a), .B(b), .O(ander_1_o));
  invuter invuter_1 (.i(a), .o(invuter_1_o));
  and and_1 (c_sl, decoder_1_out3, shl_1_so);
  SHL shl_1 (.i(a), .si(ci), .so(shl_1_so), .o(shl_1_o));
  and and_2 (c_sr, decoder_1_out2, shr_1_so);
  SHR shr_1 (.i(a), .si(ci), .so(shr_1_so), .o(shr_1_o));
  and and_3 (c_ad, adder_1_co, decoder_1_out1);
  Adder adder_1 (.Ci(ci), .A(a), .B(b), .S(adder_1_s), .Co(adder_1_co));
  Decoder #(.enable("false"), .select(3)) decoder_1 (
    .out0(decoder_1_out0), .out1(decoder_1_out1), .out2(decoder_1_out2), .out3(decoder_1_out3),
    .out4(decoder_1_out4), .out5(decoder_1_out5), .out6(decoder_1_out6), .out7(decoder_1_out7), .sel(op));
  Enabler enabler_1 (.i(xorer8_1_o), .e(decoder_1_out6), .o(out));
  Enabler enabler_2 (.i(orer_1_o), .e(decoder_1_out5), .o(out));
  Enabler enabler_3 (.i(ander_1_o), .e(decoder_1_out4), .o(out));
  Enabler enabler_4 (.i(invuter_1_o), .e(decoder_1_out3), .o(enabler_4_o));
  Enabler enabler_5 (.i(shl_1_o), .e(decoder_1_out2), .o(out));
  Enabler enabler_6 (.i(shr_1_o), .e(decoder_1_out1), .o(out));
  Enabler enabler_7 (.i(adder_1_s), .e(decoder_1_out0), .o(out));
  assign out = decoder_1_out7 ? {8{1'b0}} : 8'bz;  // Controlled_Buffer controlled_buffer_1
  Zeroer zeroer_1 (.in(out), .out(zero));
  or or_1 (co, c_sl, c_sr, c_ad);
endmodule

module test_alu (
  input  [7:0] a,
  input  [7:0] b,
  input  cin,
  input  [2:0] opcode,
  output [7:0] o,
  output out_6,
  output out_7,
  output out_8,
  output out_9
);

  ALU alu_1 (.a(a), .b(b), .ci(cin), .op(opcode), .a_b(out_8), .a_b_2(out_7), .zero(out_9), .out(o), .co(out_6));

  // Other names for the same wires on the sheet: ci = cin; op[2:0] = opcode
endmodule

module Stepper (
  input  clk,
  input  reset,
  output _1,
  output _2,
  output _3,
  output _4,
  output _5,
  output _6,
  output _7
);

  wire d_ff_1_q, d_ff_2_q, d_ff_3_q, d_ff_4_q, d_ff_5_q, d_ff_6_q, d_ff_7_q, d_ff_8_q, d_ff_9_q, d_ff_10_q,
       d_ff_11_q, not_1_out, not_2_out, not_3_out, not_4_out, not_5_out, not_6_out, not_7_out, not_8_out,
       or_1_out, or_2_out;

  not not_1 (not_1_out, _7);
  or or_1 (or_1_out, _7, clk);
  or or_2 (or_2_out, _7, not_2_out);
  not not_2 (not_2_out, clk);
  or or_3 (_1, _7, not_3_out);
  D_Flip_Flop d_ff_1 (.clk(or_1_out), .D(not_1_out), .Q(d_ff_1_q), .reset(reset));  // open: Qn, preset
  not not_3 (not_3_out, d_ff_2_q);
  D_Flip_Flop d_ff_2 (.clk(or_2_out), .D(d_ff_1_q), .Q(d_ff_2_q), .reset(reset));  // open: Qn, preset
  and and_1 (_2, d_ff_2_q, not_4_out);
  D_Flip_Flop d_ff_3 (.clk(or_1_out), .D(d_ff_2_q), .Q(d_ff_3_q), .reset(reset));  // open: Qn, preset
  not not_4 (not_4_out, d_ff_4_q);
  D_Flip_Flop d_ff_4 (.clk(or_2_out), .D(d_ff_3_q), .Q(d_ff_4_q), .reset(reset));  // open: Qn, preset
  and and_2 (_3, d_ff_4_q, not_5_out);
  D_Flip_Flop d_ff_5 (.clk(or_1_out), .D(d_ff_4_q), .Q(d_ff_5_q), .reset(reset));  // open: Qn, preset
  not not_5 (not_5_out, d_ff_6_q);
  D_Flip_Flop d_ff_6 (.clk(or_2_out), .D(d_ff_5_q), .Q(d_ff_6_q), .reset(reset));  // open: Qn, preset
  and and_3 (_4, d_ff_6_q, not_6_out);
  D_Flip_Flop d_ff_7 (.clk(or_1_out), .D(d_ff_6_q), .Q(d_ff_7_q), .reset(reset));  // open: Qn, preset
  not not_6 (not_6_out, d_ff_8_q);
  D_Flip_Flop d_ff_8 (.clk(or_2_out), .D(d_ff_7_q), .Q(d_ff_8_q), .reset(reset));  // open: Qn, preset
  and and_4 (_5, d_ff_8_q, not_7_out);
  D_Flip_Flop d_ff_9 (.clk(or_1_out), .D(d_ff_8_q), .Q(d_ff_9_q), .reset(reset));  // open: Qn, preset
  not not_7 (not_7_out, d_ff_10_q);
  D_Flip_Flop d_ff_10 (.clk(or_2_out), .D(d_ff_9_q), .Q(d_ff_10_q), .reset(reset));  // open: Qn, preset
  and and_5 (_6, d_ff_10_q, not_8_out);
  D_Flip_Flop d_ff_11 (.clk(or_1_out), .D(d_ff_10_q), .Q(d_ff_11_q), .reset(reset));  // open: Qn, preset
  not not_8 (not_8_out, _7);
  D_Flip_Flop d_ff_12 (.clk(or_2_out), .D(d_ff_11_q), .Q(_7), .reset(reset));  // open: Qn, preset
endmodule

module test_stepper (
  output out_1,
  output out_2,
  output out_3,
  output out_4,
  output out_5,
  output out_6,
  output out_7
);

  wire CLK_out;

  Clock CLK (.out(CLK_out));
  Stepper stepper_1 (
    .clk(CLK_out), .reset(out_7), ._1(out_1), ._2(out_2), ._3(out_3), ._4(out_4), ._5(out_5), ._6(out_6),
    ._7(out_7));
endmodule

module CLK (
  output clk,
  output clk_s,
  output clk_e
);

  wire clk_raw_out, j_k_ff_1_qn;

  Clock clk_raw (.out(clk_raw_out));
  J_K_Flip_Flop j_k_ff_1 (.J(1'b1), .clk(clk_raw_out), .K(1'b1), .Q(clk), .Qn(j_k_ff_1_qn));  // open: preset, reset
  and and_1 (clk_s, clk, clk_raw_out);
  and and_2 (clk_e, j_k_ff_1_qn, clk_raw_out);
endmodule

module test_AddComtrol (
  output TMP_S,
  output R0_E,
  output ACC_S,
  output R1_E,
  output R0_S,
  output ACC_E
);

  wire clk_1_clk, CLK_E, CLK_S, stepper_1__1, stepper_1__2, stepper_1__3, stepper_1__4, stepper_1__5,
       stepper_1__6, stepper_1__7;

  CLK clk_1 (.clk(clk_1_clk), .clk_s(CLK_S), .clk_e(CLK_E));
  and and_1 (R0_E, stepper_1__5, CLK_E);
  and and_2 (R1_E, stepper_1__4, CLK_E);
  and and_3 (ACC_E, stepper_1__6, CLK_E);
  LED led_1 (.in(CLK_S));
  LED led_2 (.in(CLK_E));
  LED led_3 (.in(stepper_1__1));
  LED led_4 (.in(stepper_1__2));
  LED led_5 (.in(stepper_1__3));
  LED led_6 (.in(stepper_1__4));
  LED led_7 (.in(stepper_1__5));
  LED led_8 (.in(stepper_1__6));
  Stepper stepper_1 (
    .clk(clk_1_clk), .reset(stepper_1__7), ._1(stepper_1__1), ._2(stepper_1__2), ._3(stepper_1__3),
    ._4(stepper_1__4), ._5(stepper_1__5), ._6(stepper_1__6), ._7(stepper_1__7));
  and and_4 (TMP_S, stepper_1__4, CLK_S);
  and and_5 (ACC_S, stepper_1__5, CLK_S);
  and and_6 (R0_S, stepper_1__6, CLK_S);
endmodule

module R0 (
  input  [7:0] i,
  input  s,
  input  e,
  output [7:0] o
);

  wire [7:0] register_1_q;

  Register #(.trigger("high")) register_1 (.D(i), .en(s), .Q(register_1_q), .clk(1'b1));  // open: clr
  _03_1_Enabler u_03_1_enabler_1 (.i(register_1_q), .e(e), .o(o));
endmodule

module R1 (
  input  [7:0] i,
  input  s,
  input  e,
  output [7:0] o
);

  wire [7:0] register_1_q;

  Register #(.trigger("high")) register_1 (.D(i), .en(s), .Q(register_1_q), .clk(1'b1));  // open: clr
  _03_1_Enabler u_03_1_enabler_1 (.i(register_1_q), .e(e), .o(o));
endmodule

module TMP (
  input  [7:0] i,
  input  s,
  input  e,
  output [7:0] o
);

  wire [7:0] register_1_q;

  Register #(.trigger("high")) register_1 (.D(i), .en(s), .Q(register_1_q), .clk(1'b1));  // open: clr
  _03_1_Enabler u_03_1_enabler_1 (.i(register_1_q), .e(e), .o(o));
endmodule

module ACC (
  input  [7:0] i,
  input  s,
  input  e,
  output [7:0] o
);

  wire [7:0] register_1_q;

  Register #(.trigger("high")) register_1 (.D(i), .en(s), .Q(register_1_q), .clk(1'b1));  // open: clr
  _03_1_Enabler u_03_1_enabler_1 (.i(register_1_q), .e(e), .o(o));
endmodule

module test_AddComputer (
  output [7:0] out_1
);

  wire test_addcomtrol_1_acc_e, test_addcomtrol_1_acc_s, test_addcomtrol_1_r0_e, test_addcomtrol_1_r0_s,
       test_addcomtrol_1_r1_e, test_addcomtrol_1_tmp_s;
  wire [7:0] alu_1_out, tmp_1_o;

  TMP tmp_1 (.i(out_1), .s(test_addcomtrol_1_tmp_s), .e(1'b1), .o(tmp_1_o));
  ALU alu_1 (.a(out_1), .b(tmp_1_o), .out(alu_1_out));  // open: ci, op, a_b, a_b_2, zero, co
  ACC acc_1 (.i(alu_1_out), .s(test_addcomtrol_1_acc_s), .e(test_addcomtrol_1_acc_e), .o(out_1));
  R0 r0_1 (.i(out_1), .s(test_addcomtrol_1_r0_s), .e(test_addcomtrol_1_r0_e), .o(out_1));
  R1 r1_1 (.i(out_1), .e(test_addcomtrol_1_r1_e), .o(out_1));  // open: s
  test_AddComtrol test_addcomtrol_1 (
    .TMP_S(test_addcomtrol_1_tmp_s), .R0_E(test_addcomtrol_1_r0_e), .ACC_S(test_addcomtrol_1_acc_s),
    .R1_E(test_addcomtrol_1_r1_e), .R0_S(test_addcomtrol_1_r0_s), .ACC_E(test_addcomtrol_1_acc_e));
endmodule

module R2 (
  input  [7:0] i,
  input  s,
  input  e,
  output [7:0] o
);

  wire [7:0] register_1_q;

  Register #(.trigger("high")) register_1 (.D(i), .en(s), .Q(register_1_q), .clk(1'b1));  // open: clr
  _03_1_Enabler u_03_1_enabler_1 (.i(register_1_q), .e(e), .o(o));
endmodule

module R3 (
  input  [7:0] i,
  input  s,
  input  e,
  output [7:0] o
);

  wire [7:0] register_1_q;

  Register #(.trigger("high")) register_1 (.D(i), .en(s), .Q(register_1_q), .clk(1'b1));  // open: clr
  _03_1_Enabler u_03_1_enabler_1 (.i(register_1_q), .e(e), .o(o));
endmodule

module TMP1 (
  input  [7:0] i,
  input  s,
  output [7:0] o
);

  Register #(.trigger("high")) register_1 (.D(i), .en(s), .Q(o), .clk(1'b1));  // open: clr
endmodule

module ACC1 (
  input  [7:0] i,
  input  s,
  input  e,
  output [7:0] o
);

  wire [7:0] register_1_q;

  Register #(.trigger("high")) register_1 (.D(i), .en(s), .Q(register_1_q), .clk(1'b1));  // open: clr
  _03_1_Enabler u_03_1_enabler_1 (.i(register_1_q), .e(e), .o(o));
endmodule

module test_Computer (
  output [7:0] out_1
);

  wire test_addcomtrol_1_acc_e, test_addcomtrol_1_acc_s, test_addcomtrol_1_r0_e, test_addcomtrol_1_r0_s,
       test_addcomtrol_1_r1_e, test_addcomtrol_1_tmp_s;
  wire [7:0] alu_1_out, tmp1_1_o;

  TMP1 tmp1_1 (.i(out_1), .s(test_addcomtrol_1_tmp_s), .o(tmp1_1_o));
  ALU alu_1 (.a(out_1), .b(tmp1_1_o), .out(alu_1_out));  // open: ci, op, a_b, a_b_2, zero, co
  ACC1 acc1_1 (.i(alu_1_out), .s(test_addcomtrol_1_acc_s), .e(test_addcomtrol_1_acc_e), .o(out_1));
  R0 r0_1 (.i(out_1), .s(test_addcomtrol_1_r0_s), .e(test_addcomtrol_1_r0_e), .o(out_1));
  R1 r1_1 (.i(out_1), .e(test_addcomtrol_1_r1_e), .o(out_1));  // open: s
  R2 r2_1 (.i(out_1), .o(out_1));  // open: s, e
  R3 r3_1 (.i(out_1), .o(out_1));  // open: s, e
  test_AddComtrol test_addcomtrol_1 (
    .TMP_S(test_addcomtrol_1_tmp_s), .R0_E(test_addcomtrol_1_r0_e), .ACC_S(test_addcomtrol_1_acc_s),
    .R1_E(test_addcomtrol_1_r1_e), .R0_S(test_addcomtrol_1_r0_s), .ACC_E(test_addcomtrol_1_acc_e));
endmodule

module MAR (
  input  [7:0] i,
  input  s,
  output [7:0] o
);

  Register #(.trigger("high")) register_1 (.D(i), .en(s), .Q(o), .clk(1'b1));  // open: clr
endmodule

module RAM (
  input  [7:0] a,
  input  sa,
  input  s,
  input  [7:0] i,
  input  e,
  output [7:0] o
);

  wire [7:0] controlled_buffer_1_out, mar_1_o, ram_1_dout;

  MAR mar_1 (.i(a), .s(sa), .o(mar_1_o));
  assign controlled_buffer_1_out = s ? i : 8'bz;  // Controlled_Buffer controlled_buffer_1
  assign o = e ? ram_1_dout : 8'bz;  // Controlled_Buffer controlled_buffer_2
  Hex_Digit_Display hex_digit_display_1 (.value(mar_1_o[7:4]));  // open: dp
  RAM_part #(.trigger("high")) ram_1 (
    .addr(mar_1_o), .we(s), .clk(1'b1), .din(controlled_buffer_1_out), .dout(ram_1_dout));
  Hex_Digit_Display hex_digit_display_2 (.value(mar_1_o[3:0]));  // open: dp
  Hex_Digit_Display hex_digit_display_3 (.value(ram_1_dout[7:4]));  // open: dp
  Hex_Digit_Display hex_digit_display_4 (.value(ram_1_dout[3:0]));  // open: dp
endmodule

module IAR (
  input  [7:0] i,
  input  s,
  input  e,
  output [7:0] o
);

  wire [7:0] register_1_q;

  Register #(.trigger("high")) register_1 (.D(i), .en(s), .Q(register_1_q), .clk(1'b1));  // open: clr
  _03_1_Enabler u_03_1_enabler_1 (.i(register_1_q), .e(e), .o(o));
endmodule

module IR (
  input  [7:0] i,
  input  s,
  output _0,
  output _1,
  output _2,
  output _3,
  output _4,
  output _5,
  output _6,
  output _7
);

  Register #(.trigger("high")) register_1 (
    .D(i), .en(s), .Q({_7, _6, _5, _4, _3, _2, _1, _0}), .clk(1'b1));  // open: clr
endmodule

module Bus1 (
  input  [7:0] i,
  input  bus1_e,
  output [7:0] _0
);

  wire not_1_out;

  not not_1 (not_1_out, bus1_e);
  assign _0 = not_1_out ? i : 8'bz;  // Controlled_Buffer controlled_buffer_1
  assign _0 = bus1_e ? 8'h1 : 8'bz;  // Controlled_Buffer controlled_buffer_2
endmodule

module CTMP (
  input  i,
  input  s,
  input  e,
  output o
);

  wire register_1_q;

  Register #(.trigger("high"), .width(1)) register_1 (.D(i), .en(s), .Q(register_1_q), .clk(1'b1));  // open: clr
  and and_1 (o, register_1_q, e);
endmodule

module Flags (
  input  i_4,
  input  i_5,
  input  i_6,
  input  i_7,
  input  s,
  output _0_4,
  output _0_5,
  output _0_6,
  output _0_7
);

  wire [3:0] register_1_q;

  Register #(.trigger("high")) register_1 (
    .D({i_7, i_6, i_5, i_4, 4'b0000}), .en(s), .Q({_0_7, _0_6, _0_5, _0_4, register_1_q}), .clk(1'b1));  // open: clr
endmodule

module ControlUnit1 (
  input  F4,
  input  F5,
  input  F6,
  input  F7,
  input  _0,
  input  _1,
  input  _2,
  input  _3,
  input  _4,
  input  _5,
  input  _6,
  input  _7,
  output BUS1_E,
  output MAR_S,
  output R0_E,
  output R0_S,
  output IAR_E,
  output IR_S,
  output R1_E,
  output R1_S,
  output RAM_E,
  output IAR_S,
  output R2_E,
  output R2_S,
  output ACC_E,
  output ACC_S,
  output R3_E,
  output R3_S,
  output TMP_S,
  output RAM_S,
  output CL_E,
  output FLAGS_S,
  output [2:0] op_out
);

  wire clk_1_clk, CLK_E, CLK_S, S1, S2, S3, S4, S5, S6, stepper_1__7;

  CLK clk_1 (.clk(clk_1_clk), .clk_s(CLK_S), .clk_e(CLK_E));
  LED led_1 (.in(CLK_E));
  LED led_2 (.in(S1));
  LED led_3 (.in(S2));
  LED led_4 (.in(S3));
  LED led_5 (.in(S4));
  LED led_6 (.in(S5));
  LED led_7 (.in(S6));
  Stepper stepper_1 (
    .clk(clk_1_clk), .reset(stepper_1__7), ._1(S1), ._2(S2), ._3(S3), ._4(S4), ._5(S5), ._6(S6),
    ._7(stepper_1__7));
  LED led_8 (.in(CLK_S));

  // Notes on the sheet:
  //   [ Stepper Module ]
  //   [ IR Code Module ]
endmodule
